# Fritzing sketch Schema_Seeduino_Xiao (saved by Fritzing 0.9.9b)
breadboards: 1

parts:
  DFRobot_DFPlayer_Mini1 = DFRobot DFPlayer Mini [part_number=DFR0299]
  SP1 = SPEAKER [package=pcb_mount_speaker]  # not connected
  S1 = SWITCH-MOMENTARY-2 [package=tactile-switch-1101ne]  # not connected
  Mod1 = seeeduino-xiao_1

nets:
  N1: DFRobot_DFPlayer_Mini1.RX, Mod1.connector13

notes:
  Détection décrochage
  Combiné
  (masse globale)
  B
  C
  Cadran rotatif
  Seeduino
  Xiao
  DFPlayer
  (Lecteur MP3)
  E
  F
  H
  G
